# Fritzing sketch ultrasonic (saved by Fritzing 0.9.5d)
breadboards: 1

parts:
  Eris_Dev_Kit_v1_r1 = Eris Dev Kit v1 r2 [package=LQFP-48]
  HC-SR04_Sensor_1 = HC-SR04 Ultrasonic Distance Sensor

nets:
  N1: Eris_Dev_Kit_v1_r1.PB11/RX3, HC-SR04_Sensor_1.ECHO
  N2: Eris_Dev_Kit_v1_r1.PB10/TX3, HC-SR04_Sensor_1.TRIG
  N3: Eris_Dev_Kit_v1_r1.5V_1, HC-SR04_Sensor_1.VCC
  N4: Eris_Dev_Kit_v1_r1.GND_2, HC-SR04_Sensor_1.GND

custom parts:
  Eris Dev Kit v1 r2: Africa's Talking Eris Development Kit version 1 revision 2
