# Fritzing sketch 7analog_writing_voltages_gradually_light_led (saved by Fritzing 0.9.5d)
breadboards: 1

parts:
  Eris_Dev_Kit_v1_r1 = Eris Dev Kit v1 r2 [package=LQFP-48]
  LED1 = LED - 5mm [color="White (8000K)" package="5 mm [THT]"]
  LED2 = LED - 5mm [color="Blue (430nm)" package="5 mm [THT]"]
  R1 = Resistor [tolerance=±5% resistance=220 package=THT]
  R3 = Resistor [tolerance=±5% resistance=220 package=THT]

nets:
  N1: Eris_Dev_Kit_v1_r1.PA6, R1.Pin_1
  N2: Eris_Dev_Kit_v1_r1.PA7, R3.Pin_1
  N3: Eris_Dev_Kit_v1_r1.GND_7, LED1.cathode, LED2.cathode
  N4: LED1.anode, R3.Pin_0
  N5: LED2.anode, R1.Pin_0

custom parts:
  Eris Dev Kit v1 r2: Africa's Talking Eris Development Kit version 1 revision 2
