# Fritzing sketch turningon (saved by Fritzing 0.9.5d)
breadboards: 1

parts:
  Eris_Dev_Kit_v1_r1 = Eris Dev Kit v1 r2 [package=LQFP-48]
  LED1 = LED - 5mm [color="Red (633nm)" package="5 mm [THT]"]
  R1 = Resistor [tolerance=±5% resistance=220 package=THT]

nets:
  N1: Eris_Dev_Kit_v1_r1.PA7, R1.Pin_1
  N2: Eris_Dev_Kit_v1_r1.GND_7, LED1.cathode
  N3: LED1.anode, R1.Pin_0

custom parts:
  Eris Dev Kit v1 r2: Africa's Talking Eris Development Kit version 1 revision 2
