# Fritzing sketch buzzer (saved by Fritzing 0.9.5d)
breadboards: 1

parts:
  Eris_Dev_Kit_v1_r1 = Eris Dev Kit v1 r2 [package=LQFP-48]
  Mod1 = Passive Buzzer

nets:
  N1: Eris_Dev_Kit_v1_r1.PA7, Mod1.NC
  N2: Eris_Dev_Kit_v1_r1.5V_6, Mod1.S
  N3: Eris_Dev_Kit_v1_r1.GND_7, Mod1.-

custom parts:
  Eris Dev Kit v1 r2: Africa's Talking Eris Development Kit version 1 revision 2
