# Fritzing sketch ldr (saved by Fritzing 0.9.5d)
breadboards: 1

parts:
  Eris_Dev_Kit_v1_r1 = Eris Dev Kit v1 r2 [package=LQFP-48]
  R2 = Photocell (LDR) [package=THT]

nets:
  N1: Eris_Dev_Kit_v1_r1.PA6, R2.pin_1
  N2: Eris_Dev_Kit_v1_r1.GND_7, R2.pin_0

custom parts:
  Eris Dev Kit v1 r2: Africa's Talking Eris Development Kit version 1 revision 2
