# Fritzing sketch moisturesensor (saved by Fritzing 0.9.5d)

parts:
  Eris_Dev_Kit_v1_r1 = Eris Dev Kit v1 r2 [package=LQFP-48]
  Part1 = Soil Moisture Sensor

nets:
  N1: Eris_Dev_Kit_v1_r1.PA6, Part1.SIG
  N2: Eris_Dev_Kit_v1_r1.5V_5, Part1.VCC
  N3: Eris_Dev_Kit_v1_r1.GND_6, Part1.GND

custom parts:
  Eris Dev Kit v1 r2: Africa's Talking Eris Development Kit version 1 revision 2
