# Fritzing sketch trafficlights (saved by Fritzing 0.9.5d)
breadboards: 1

parts:
  Eris_Dev_Kit_v1_r1 = Eris Dev Kit v1 r2 [package=LQFP-48]
  LED1 = LED - 5mm [color="Red (633nm)" package="5 mm [THT]"]
  LED2 = LED - 5mm [color="Orange (612nm)" package="5 mm [THT]"]
  LED3 = LED - 5mm [color="Green (565nm)" package="5 mm [THT]"]
  R1 = Resistor [tolerance=±5% resistance=220 package=THT]
  R2 = Resistor [tolerance=±5% resistance=220 package=THT]
  R3 = Resistor [tolerance=±5% resistance=220 package=THT]

nets:
  N1: Eris_Dev_Kit_v1_r1.PA6, R1.Pin_1
  N2: Eris_Dev_Kit_v1_r1.PB1, R2.Pin_1
  N3: Eris_Dev_Kit_v1_r1.PA7, R3.Pin_1
  N4: Eris_Dev_Kit_v1_r1.GND_7, LED1.cathode, LED2.cathode, LED3.cathode
  N5: LED1.anode, R3.Pin_0
  N6: LED2.anode, R1.Pin_0
  N7: LED3.anode, R2.Pin_0

custom parts:
  Eris Dev Kit v1 r2: Africa's Talking Eris Development Kit version 1 revision 2
