# Fritzing sketch dimmingled (saved by Fritzing 0.9.5d)
breadboards: 1

parts:
  Eris_Dev_Kit_v1_r1 = Eris Dev Kit v1 r2 [package=LQFP-48]
  U1 = POT [package=pot_mammoth]
  R1 = Resistor [tolerance=±5% resistance=220 package=THT]
  LED1 = LED - 5mm [color="Red (633nm)" package="5 mm [THT]"]

nets:
  N1: Eris_Dev_Kit_v1_r1.PA6, R1.Pin_1
  N2: Eris_Dev_Kit_v1_r1.PA7, U1.A
  N3: Eris_Dev_Kit_v1_r1.5V_6, U1.E
  N4: Eris_Dev_Kit_v1_r1.GND_7, U1.S, LED1.cathode
  N5: R1.Pin_0, LED1.anode

custom parts:
  Eris Dev Kit v1 r2: Africa's Talking Eris Development Kit version 1 revision 2
