# Fritzing sketch potentiometer (saved by Fritzing 0.9.5d)
breadboards: 1

parts:
  Eris_Dev_Kit_v1_r1 = Eris Dev Kit v1 r2 [package=LQFP-48]
  U1 = POT [package=pot_mammoth]

nets:
  N1: Eris_Dev_Kit_v1_r1.PA7, U1.A
  N2: Eris_Dev_Kit_v1_r1.5V_6, U1.E
  N3: Eris_Dev_Kit_v1_r1.GND_7, U1.S

custom parts:
  Eris Dev Kit v1 r2: Africa's Talking Eris Development Kit version 1 revision 2
