# Fritzing sketch dht11 (saved by Fritzing 0.9.5d)
breadboards: 1

parts:
  Eris_Dev_Kit_v1_r1 = Eris Dev Kit v1 r2 [package=LQFP-48]
  DHT11_1 = DHT11 module

nets:
  N1: Eris_Dev_Kit_v1_r1.PA6, DHT11_1.DATA
  N2: Eris_Dev_Kit_v1_r1.5V_5, DHT11_1.VCC
  N3: Eris_Dev_Kit_v1_r1.GND_6, DHT11_1.GND

custom parts:
  Eris Dev Kit v1 r2: Africa's Talking Eris Development Kit version 1 revision 2
  DHT11 module: DHT11 black pcb module
